# Fritzing sketch sound (saved by Fritzing 1.0.0rc)
breadboards: 1

parts:
  Part4 = Adafruit MAX9814 Electret Microphone Amplifier [part_number="Adafruit #1713"]
  Part5 = Adafruit ESP32 Feather V2

nets:
  GND: Part4.GND, Part5.GND, Part5.SDA, Part5.IO27_A10
  VDD: Part4.VDD, Part5.3.3V
  N1: Part4.OUTPUT, Part5.A2_I34

custom parts:
  Adafruit MAX9814 Electret Microphone Amplifier: Add an ear to your project with this well-designed electret microphone amplifier with AGC. This fully assembled and tested board comes with a 20-20KHz electret microphone soldered on. For the amplification, we use the Maxim MAX9814, a specialty chip that is designed for amplifying electret microphones in situations where the loudness of the audio isn't predictable. This fancy microphone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
